// Logisim project MileStone1_Team123.circ as structural Verilog: 1 circuit, main circuit main
module main (
  input  [2:0] Select_Lines,
  input  in_2,
  input  in_3,
  input  in_4,
  input  in_5,
  input  in_6,
  input  in_7,
  input  in_8,
  input  in_9,
  input  in_10,
  input  in_11,
  input  in_12,
  input  [2:0] in_13,
  input  in_14
);

  wire clock_1_out;
  wire [5:0] AR_q, bit_extender_1_out, bit_extender_3_out, PC_q;
  wire [15:0] AC_q, adder_1_out, and_1_out, bit_extender_2_out, bit_extender_4_out, DR_q, IR_q,
       multiplexer_1_out, multiplexer_2_out, not_1_out, or_1_out, ram_1_data, subtractor_1_out, TR_q,
       xor_1_out;

  Subtractor #(.width(16)) subtractor_1 (.a(AC_q), .b(DR_q), .out(subtractor_1_out), .bin(in_11));  // open: bout
  Adder #(.width(16)) adder_1 (.a(AC_q), .b(DR_q), .out(adder_1_out), .cin(in_12));  // open: cout
  assign and_1_out = AC_q & DR_q;  // AND_Gate and_1, 16 bits wide
  RAM #(.addrWidth(6), .dataWidth(16), .bus("separate")) ram_1 (
    .addr(AR_q), .din(multiplexer_2_out), .data(ram_1_data), .str(in_9), .clk(clock_1_out), .ld(in_10));  // open: sel, clr
  assign or_1_out = AC_q | DR_q;  // OR_Gate or_1, 16 bits wide
  Register #(.width(16)) IR (.D(multiplexer_2_out), .en(in_3), .Q(IR_q), .clk(clock_1_out));  // open: clr
  assign not_1_out = ~AC_q;  // NOT_Gate not_1, 16 bits wide
  assign xor_1_out = AC_q ^ DR_q;  // XOR_Gate xor_1, 16 bits wide
  Bit_Extender #(.in_width(16), .out_width(6)) bit_extender_1 (.in(multiplexer_2_out), .out(bit_extender_1_out));
  Multiplexer #(.select(3), .width(16)) multiplexer_1 (
    .in0(adder_1_out), .in1(subtractor_1_out), .in2(DR_q), .in3(and_1_out), .in4(or_1_out), .in5(xor_1_out),
    .in6(not_1_out), .out(multiplexer_1_out), .sel(in_13), .en(in_14));  // open: in7
  Counter #(.width(6), .max('h3f)) PC (
    .load(in_4), .D(bit_extender_1_out), .Q(PC_q), .clk(clock_1_out));  // open: count, carry, clr
  assign bit_extender_2_out = {{10{1'b0}}, PC_q};  // Bit_Extender bit_extender_2
  Register #(.width(16)) AC (.D(multiplexer_1_out), .en(in_5), .Q(AC_q), .clk(clock_1_out));  // open: clr
  Register #(.width(16)) DR (.D(multiplexer_2_out), .en(in_6), .Q(DR_q), .clk(clock_1_out));  // open: clr
  Register #(.width(16)) TR (.D(multiplexer_2_out), .en(in_7), .Q(TR_q), .clk(clock_1_out));  // open: clr
  Bit_Extender #(.in_width(16), .out_width(6)) bit_extender_3 (.in(multiplexer_2_out), .out(bit_extender_3_out));
  Register #(.width(6)) AR (.D(bit_extender_3_out), .en(in_8), .Q(AR_q), .clk(clock_1_out));  // open: clr
  Multiplexer #(.select(3), .width(16)) multiplexer_2 (
    .in0(AC_q), .in1(DR_q), .in2(TR_q), .in3(bit_extender_4_out), .in4(ram_1_data), .in5(bit_extender_2_out),
    .in6(IR_q), .out(multiplexer_2_out), .sel(Select_Lines), .en(in_2));  // open: in7
  assign bit_extender_4_out = {{10{1'b0}}, AR_q};  // Bit_Extender bit_extender_4
  Clock clock_1 (.out(clock_1_out));
endmodule
